// Logisim project CPS 213 Lab 05 mux ver.circ as structural Verilog: 14 circuits, main circuit Arithmetic Logic Unit
module Arithmetic_Logic_Unit (
  input  Cin_add,
  input  Cin_sub,
  input  [3:0] A,
  input  [1:0] Selector,
  input  [3:0] B,
  input  Mode
);

  wire _7_Segment_decoder_a, _7_Segment_decoder_b, _7_Segment_decoder_c, _7_Segment_decoder_d,
       _7_Segment_decoder_e, _7_Segment_decoder_f, _7_Segment_decoder_g, Arithmetic_Unit_carry_out,
       Arithmetic_Unit_carry_out__sub, Comparator_a_b, Comparator_a_b_2, Comparator_a_b_3;
  wire [3:0] Arithmetic_Unit_out_8, demultiplexer_1_out0, demultiplexer_1_out1, Logic_Unit_out_4,
       multiplexer_1_out;

  Arithmetic_Unit Arithmetic_Unit (
    .A(A), .B(B), .Selector(Selector), .Carry_In(Cin_add), .Carry_Out(Arithmetic_Unit_carry_out),
    .Carry_In_SUB(Cin_sub), .Carry_Out__SUB(Arithmetic_Unit_carry_out__sub), .out_8(Arithmetic_Unit_out_8));
  Logic_Unit Logic_Unit (.A(A), .B(B), .out_4(Logic_Unit_out_4), .Selector(Selector));
  _4_bit_Comparator Comparator (.A(A), .B(B), .A_B(Comparator_a_b), .A_B_2(Comparator_a_b_2), .A_B_3(Comparator_a_b_3));
  LED Cout_add (.in(Arithmetic_Unit_carry_out));
  LED A_B (.in(Comparator_a_b));
  LED A_B_2 (.in(Comparator_a_b_2));
  LED A_B_3 (.in(Comparator_a_b_3));
  LED Cout_sub (.in(Arithmetic_Unit_carry_out__sub));
  Multiplexer #(.width(4), .enable("false")) multiplexer_1 (
    .in0(Arithmetic_Unit_out_8), .in1(Logic_Unit_out_4), .out(multiplexer_1_out), .sel(Mode));
  Demultiplexer #(.width(4), .enable("false")) demultiplexer_1 (
    .out0(demultiplexer_1_out0), .out1(demultiplexer_1_out1), .in(multiplexer_1_out), .sel(Mode));
  _7_Segement_decoder _7_Segment_decoder (
    .W(demultiplexer_1_out0[3]), .X(demultiplexer_1_out0[2]), .Y(demultiplexer_1_out0[1]),
    .Z(demultiplexer_1_out0[0]), .a(_7_Segment_decoder_a), .b(_7_Segment_decoder_b),
    .c(_7_Segment_decoder_c), .d(_7_Segment_decoder_d), .e(_7_Segment_decoder_e), .f(_7_Segment_decoder_f),
    .g(_7_Segment_decoder_g));
  _7_Segment_Display u_7_segment_display_1 (
    .g(_7_Segment_decoder_g), .f(_7_Segment_decoder_f), .a(_7_Segment_decoder_a), .b(_7_Segment_decoder_b),
    .e(_7_Segment_decoder_e), .d(_7_Segment_decoder_d), .c(_7_Segment_decoder_c));  // open: dp
  DotMatrix #(.matrixcols(4), .matrixrows(1)) dotmatrix_1 (
    .col0(demultiplexer_1_out1[3]), .col1(demultiplexer_1_out1[2]), .col2(demultiplexer_1_out1[1]),
    .col3(demultiplexer_1_out1[0]));
endmodule

module _4_bit_Adder (
  input  Carry_in,
  input  [3:0] A,
  input  [3:0] B,
  output [3:0] Sum,
  output Carry_out
);

  wire adder_1_cout, adder_2_cout, adder_3_cout;

  Adder #(.width(1)) adder_1 (.a(A[0]), .b(B[0]), .out(Sum[0]), .cin(Carry_in), .cout(adder_1_cout));
  Adder #(.width(1)) adder_2 (.a(A[1]), .b(B[1]), .out(Sum[1]), .cin(adder_1_cout), .cout(adder_2_cout));
  Adder #(.width(1)) adder_3 (.a(A[2]), .b(B[2]), .out(Sum[2]), .cin(adder_2_cout), .cout(adder_3_cout));
  Adder #(.width(1)) adder_4 (.a(A[3]), .b(B[3]), .out(Sum[3]), .cin(adder_3_cout), .cout(Carry_out));
endmodule

module _4_bit_Subtractor (
  input  Cin,
  input  [3:0] A,
  input  [3:0] B,
  output [3:0] Sub,
  output C_out
);

  Subtractor #(.width(4)) subtractor_1 (.a(A), .b(B), .out(Sub), .bin(Cin), .bout(C_out));
endmodule

module _2_s_Complement (
  input  [3:0] B,
  output [3:0] _2_s_Comp
);

  wire [3:0] _1_s_Comp_out_2;

  _1_s_Complement _1_s_Comp (.in_1(B), .out_2(_1_s_Comp_out_2));
  _4_bit_Adder _4_Bit_Adder (.A(_1_s_Comp_out_2), .B(4'b0001), .Sum(_2_s_Comp));  // open: Carry_in, Carry_out
endmodule

module Incrementor (
  input  [3:0] A,
  output [3:0] out_2
);

  wire adder_1_cout, adder_2_cout, adder_3_cout, adder_4_cout;

  Adder #(.width(1)) adder_1 (.a(A[0]), .b(1'b1), .out(out_2[0]), .cout(adder_1_cout));  // open: cin
  Adder #(.width(1)) adder_2 (.a(A[1]), .b(adder_1_cout), .out(out_2[1]), .cout(adder_2_cout));  // open: cin
  Adder #(.width(1)) adder_3 (.a(A[2]), .b(adder_2_cout), .out(out_2[2]), .cout(adder_3_cout));  // open: cin
  Adder #(.width(1)) adder_4 (.a(A[3]), .b(adder_3_cout), .out(out_2[3]), .cout(adder_4_cout));  // open: cin
  LED Carry_out (.in(adder_4_cout));
endmodule

module Arithmetic_Unit (
  input  Carry_In,
  input  [3:0] A,
  input  [3:0] B,
  input  Carry_In_SUB,
  input  [1:0] Selector,
  output Carry_Out,
  output Carry_Out__SUB,
  output [3:0] out_8
);

  wire [3:0] _2_s_Comp__2_s_comp, Adder_sum, Incrementor_out_2, Subtractor_sub;

  _4_bit_Adder Adder (.A(A), .B(B), .Carry_in(Carry_In), .Carry_out(Carry_Out), .Sum(Adder_sum));
  _4_bit_Subtractor Subtractor (.A(A), .B(B), .Cin(Carry_In_SUB), .C_out(Carry_Out__SUB), .Sub(Subtractor_sub));
  _2_s_Complement _2_s_Comp (.B(B), ._2_s_Comp(_2_s_Comp__2_s_comp));
  Incrementor Incrementor (.A(A), .out_2(Incrementor_out_2));
  Multiplexer #(.select(2), .width(4), .enable("false")) multiplexer_1 (
    .in0(Adder_sum), .in1(Subtractor_sub), .in2(_2_s_Comp__2_s_comp), .in3(Incrementor_out_2), .out(out_8),
    .sel(Selector));
endmodule

module OR (
  input  [3:0] A,
  input  [3:0] B,
  output [3:0] Result
);

  or or_1 (Result[0], A[0], B[0]);
  or or_2 (Result[1], A[1], B[1]);
  or or_3 (Result[2], A[2], B[2]);
  or or_4 (Result[3], A[3], B[3]);
endmodule

module AND (
  input  [3:0] A,
  input  [3:0] B,
  output [3:0] Result
);

  and and_1 (Result[0], A[0], B[0]);
  and and_2 (Result[1], A[1], B[1]);
  and and_3 (Result[2], A[2], B[2]);
  and and_4 (Result[3], A[3], B[3]);
endmodule

module XOR (
  input  [3:0] A,
  input  [3:0] B,
  output [3:0] Output
);

  xor xor_1 (Output[0], A[0], B[0]);
  xor xor_2 (Output[1], A[1], B[1]);
  xor xor_3 (Output[2], A[2], B[2]);
  xor xor_4 (Output[3], A[3], B[3]);
endmodule

module _4_bit_Comparator (
  input  [3:0] A,
  input  [3:0] B,
  output A_B,
  output A_B_2,
  output A_B_3
);

  wire AND_2_out, AND_3_out, AND_4_out, AND_5_out, AND_6_out, AND_7_out, AND_8_out, AND_9_out, AND_10_out,
       AND_11_out, AND_12_out, AND_13_out, AND_14_out, AND_out, NOR_2_out, NOR_3_out, NOR_4_out, NOR_out,
       not_1_out, not_2_out, not_3_out, not_4_out, not_5_out, not_6_out, not_7_out, not_8_out;

  not not_1 (not_1_out, A[0]);
  not not_2 (not_2_out, B[0]);
  not not_3 (not_3_out, A[1]);
  not not_4 (not_4_out, B[1]);
  not not_5 (not_5_out, A[2]);
  not not_6 (not_6_out, B[2]);
  not not_7 (not_7_out, A[3]);
  not not_8 (not_8_out, B[3]);
  and AND (AND_out, not_1_out, B[0]);
  and AND_2 (AND_2_out, A[0], not_2_out);
  and AND_3 (AND_3_out, not_3_out, B[1]);
  and AND_4 (AND_4_out, A[1], not_4_out);
  and AND_5 (AND_5_out, not_5_out, B[2]);
  and AND_6 (AND_6_out, A[2], not_6_out);
  and AND_7 (AND_7_out, not_7_out, B[3]);
  and AND_8 (AND_8_out, A[3], not_8_out);
  nor NOR (NOR_out, AND_out, AND_2_out);
  nor NOR_2 (NOR_2_out, AND_3_out, AND_4_out);
  nor NOR_3 (NOR_3_out, AND_5_out, AND_6_out);
  nor NOR_4 (NOR_4_out, AND_7_out, AND_8_out);
  and AND_9 (AND_9_out, NOR_4_out, AND_6_out);
  and AND_10 (AND_10_out, NOR_4_out, NOR_3_out, AND_4_out);
  and AND_11 (AND_11_out, NOR_4_out, NOR_3_out, NOR_2_out, AND_2_out);
  and AND_12 (AND_12_out, AND_5_out, NOR_4_out);
  and AND_13 (AND_13_out, NOR_4_out, NOR_3_out, AND_3_out);
  and AND_14 (AND_14_out, NOR_3_out, NOR_4_out, NOR_2_out, AND_out);
  or OR (A_B_3, AND_8_out, AND_9_out, AND_10_out, AND_11_out);
  and AND_15 (A_B_2, NOR_out, NOR_2_out, NOR_3_out, NOR_4_out);
  or OR_2 (A_B, AND_7_out, AND_12_out, AND_13_out, AND_14_out);
endmodule

module Logic_Unit (
  input  [3:0] A,
  input  [3:0] B,
  input  [1:0] Selector,
  output [3:0] out_4
);

  wire [3:0] _1_s_Comp_out_2, AND_result, OR_result, XOR_output;

  AND AND (.A(A), .B(B), .Result(AND_result));
  OR OR (.A(A), .B(B), .Result(OR_result));
  XOR XOR (.A(A), .B(B), .Output(XOR_output));
  _1_s_Complement _1_s_Comp (.in_1(A), .out_2(_1_s_Comp_out_2));
  Multiplexer #(.select(2), .width(4), .enable("false")) multiplexer_1 (
    .in0(AND_result), .in1(OR_result), .in2(XOR_output), .in3(_1_s_Comp_out_2), .out(out_4), .sel(Selector));
endmodule

module _1_s_Complement (
  input  [3:0] in_1,
  output [3:0] out_2
);

  not not_1 (out_2[0], in_1[0]);
  not not_2 (out_2[1], in_1[1]);
  not not_3 (out_2[2], in_1[2]);
  not not_4 (out_2[3], in_1[3]);
endmodule

module _7_Segement_decoder (
  input  W,
  input  X,
  input  Y,
  input  Z,
  output a,
  output b,
  output c,
  output d,
  output e,
  output f,
  output g
);

  wire and_1_out, and_2_out, and_3_out, and_4_out, and_5_out, and_6_out, and_7_out, and_8_out, and_9_out,
       and_10_out, and_11_out, and_12_out, and_13_out, and_14_out, and_15_out, and_16_out, and_17_out,
       and_18_out, and_19_out, and_20_out, and_21_out, and_22_out, and_23_out, and_24_out, and_25_out,
       and_26_out, and_27_out, and_28_out, and_29_out, and_30_out, and_31_out, and_32_out, and_33_out,
       and_34_out, and_35_out, not_1_out, not_2_out, not_3_out, not_4_out, not_5_out, not_6_out, not_7_out,
       not_8_out, not_9_out, not_10_out, not_11_out, not_12_out, not_13_out, not_14_out, not_15_out,
       not_16_out, not_17_out, not_18_out, not_19_out, not_20_out, not_21_out, not_22_out, not_23_out,
       not_24_out, not_25_out, not_26_out, not_27_out, not_28_out, not_29_out, not_30_out, not_31_out,
       not_32_out, not_33_out, not_34_out, not_35_out, not_36_out, not_37_out, not_38_out, not_39_out,
       not_40_out, not_41_out, not_42_out, not_43_out;

  not not_1 (not_1_out, X);
  and and_1 (and_1_out, not_1_out, not_2_out);
  not not_2 (not_2_out, Z);
  not not_3 (not_3_out, W);
  and and_2 (and_2_out, not_3_out, Y);
  not not_4 (not_4_out, W);
  and and_3 (and_3_out, not_4_out, X, Z);
  and and_4 (and_4_out, X, Y);
  not not_5 (not_5_out, X);
  and and_5 (and_5_out, W, not_5_out, not_6_out);
  not not_6 (not_6_out, Y);
  and and_6 (and_6_out, W, not_7_out);
  not not_7 (not_7_out, Z);
  not not_8 (not_8_out, W);
  and and_7 (and_7_out, not_8_out, not_9_out);
  not not_9 (not_9_out, X);
  not not_10 (not_10_out, W);
  and and_8 (and_8_out, not_10_out, not_11_out, not_12_out);
  not not_11 (not_11_out, Y);
  not not_12 (not_12_out, Z);
  not not_13 (not_13_out, X);
  and and_9 (and_9_out, not_13_out, not_14_out);
  not not_14 (not_14_out, Z);
  not not_15 (not_15_out, W);
  and and_10 (and_10_out, not_15_out, Y, Z);
  and and_11 (and_11_out, W, not_16_out, Z);
  not not_16 (not_16_out, Y);
  not not_17 (not_17_out, W);
  and and_12 (and_12_out, not_17_out, not_18_out);
  not not_18 (not_18_out, Y);
  not not_19 (not_19_out, W);
  and and_13 (and_13_out, not_19_out, Z);
  not not_20 (not_20_out, Y);
  and and_14 (and_14_out, not_20_out, Z);
  not not_21 (not_21_out, W);
  and and_15 (and_15_out, not_21_out, X);
  and and_16 (and_16_out, W, not_22_out);
  not not_22 (not_22_out, X);
  not not_23 (not_23_out, W);
  and and_17 (and_17_out, not_23_out, not_24_out, not_25_out);
  not not_24 (not_24_out, X);
  not not_25 (not_25_out, Z);
  not not_26 (not_26_out, X);
  and and_18 (and_18_out, not_26_out, Y, Z);
  not not_27 (not_27_out, Y);
  and and_19 (and_19_out, X, not_27_out, Z);
  and and_20 (and_20_out, X, Y, not_28_out);
  not not_28 (not_28_out, Z);
  and and_21 (and_21_out, W, not_29_out);
  not not_29 (not_29_out, Y);
  not not_30 (not_30_out, X);
  and and_22 (and_22_out, not_30_out, not_31_out);
  not not_31 (not_31_out, Z);
  and and_23 (and_23_out, Y, not_32_out);
  not not_32 (not_32_out, Z);
  and and_24 (and_24_out, W, Y);
  and and_25 (and_25_out, W, X);
  not not_33 (not_33_out, Y);
  and and_26 (and_26_out, not_33_out, not_34_out);
  not not_34 (not_34_out, Z);
  not not_35 (not_35_out, W);
  and and_27 (and_27_out, not_35_out, X, not_36_out);
  not not_36 (not_36_out, Y);
  and and_28 (and_28_out, X, not_37_out);
  not not_37 (not_37_out, Z);
  and and_29 (and_29_out, W, not_38_out);
  not not_38 (not_38_out, X);
  and and_30 (and_30_out, W, Y);
  not not_39 (not_39_out, X);
  and and_31 (and_31_out, not_39_out, Y);
  and and_32 (and_32_out, Y, not_40_out);
  not not_40 (not_40_out, Z);
  not not_41 (not_41_out, W);
  and and_33 (and_33_out, not_41_out, X, not_42_out);
  not not_42 (not_42_out, Y);
  and and_34 (and_34_out, W, not_43_out);
  not not_43 (not_43_out, X);
  and and_35 (and_35_out, W, Z);
  or or_1 (b, and_7_out, and_8_out, and_9_out, and_10_out, and_11_out);
  or or_2 (c, and_12_out, and_13_out, and_14_out, and_15_out, and_16_out);
  or or_3 (d, and_17_out, and_18_out, and_19_out, and_20_out, and_21_out);
  or or_4 (e, and_22_out, and_23_out, and_24_out, and_25_out);
  or or_5 (f, and_26_out, and_27_out, and_28_out, and_29_out, and_30_out);
  or or_6 (g, and_31_out, and_32_out, and_33_out, and_34_out, and_35_out);
  or or_7 (a, and_1_out, and_2_out, and_3_out, and_4_out, and_5_out, and_6_out);
endmodule

module MUX (
  input  in_1,
  input  in_2,
  input  in_3,
  input  in_4,
  input  [1:0] in_5,
  output out_6
);

  wire and_1_out, and_2_out, and_3_out, and_4_out, not_1_out, not_2_out;

  not not_1 (not_1_out, in_5[1]);
  not not_2 (not_2_out, in_5[0]);
  and and_1 (and_1_out, in_1, not_1_out, not_2_out);
  and and_2 (and_2_out, in_2, not_1_out, in_5[0]);
  and and_3 (and_3_out, in_3, in_5[1], not_2_out);
  and and_4 (and_4_out, in_4, in_5[1], in_5[0]);
  or or_1 (out_6, and_1_out, and_2_out, and_3_out, and_4_out);
endmodule
