// Logisim project Lab 1.circ as structural Verilog: 8 circuits, main circuit OR
module OR (
  input  [3:0] A,
  input  [3:0] B,
  output [3:0] Result
);

  or or_1 (Result[0], A[0], B[0]);
  or or_2 (Result[1], A[1], B[1]);
  or or_3 (Result[2], A[2], B[2]);
  or or_4 (Result[3], A[3], B[3]);
endmodule

module AND (
  input  [3:0] A,
  input  [3:0] B,
  output [3:0] Result
);

  and and_1 (Result[0], A[0], B[0]);
  and and_2 (Result[1], A[1], B[1]);
  and and_3 (Result[2], A[2], B[2]);
  and and_4 (Result[3], A[3], B[3]);
endmodule

module Logic (
  input  [3:0] A,
  input  [3:0] B,
  input  in_3,
  output [3:0] C
);

  wire [3:0] AND_result, OR_result;

  AND AND (.A(A), .B(B), .Result(AND_result));
  OR OR (.A(A), .B(B), .Result(OR_result));
  Multiplexer #(.width(4), .enable("false")) multiplexer_1 (.in0(AND_result), .in1(OR_result), .out(C), .sel(in_3));
endmodule

module Adder (
  input  [3:0] A,
  input  [3:0] B,
  output [3:0] Sum,
  output Carry_out
);

  wire adder_1_cout, adder_2_cout, adder_3_cout;

  Adder_part #(.width(1)) adder_1 (.a(A[0]), .b(B[0]), .out(Sum[0]), .cout(adder_1_cout));  // open: cin
  Adder_part #(.width(1)) adder_2 (.a(A[1]), .b(B[1]), .out(Sum[1]), .cin(adder_1_cout), .cout(adder_2_cout));
  Adder_part #(.width(1)) adder_3 (.a(A[2]), .b(B[2]), .out(Sum[2]), .cin(adder_2_cout), .cout(adder_3_cout));
  Adder_part #(.width(1)) adder_4 (.a(A[3]), .b(B[3]), .out(Sum[3]), .cin(adder_3_cout), .cout(Carry_out));
endmodule

module Subtracter (
  input  [3:0] A,
  input  [3:0] B,
  output [3:0] Sub,
  output C_out
);

  Subtractor #(.width(4)) subtractor_1 (.a(A), .b(B), .out(Sub), .bout(C_out));  // open: bin
endmodule

module Arithmetic (
  input  [3:0] A,
  input  in_2,
  input  [3:0] B,
  output out_4,
  output [3:0] C,
  output out_6
);

  wire [3:0] Adder_sum, Subtractor_sub;

  Adder Adder (.A(A), .B(B), .Carry_out(out_4), .Sum(Adder_sum));
  Subtracter Subtractor (.A(A), .B(B), .C_out(out_6), .Sub(Subtractor_sub));
  Multiplexer #(.width(4), .enable("false")) multiplexer_1 (.in0(Adder_sum), .in1(Subtractor_sub), .out(C), .sel(in_2));
endmodule

module ALU_MK_II (
  input  [3:0] A,
  input  in_2,
  input  in_3,
  input  [3:0] B,
  input  in_5,
  input  in_6,
  input  in_7
);

  wire _7_segment_a, _7_segment_b, _7_segment_c, _7_segment_d, _7_segment_e, _7_segment_f, _7_segment_g,
       AU_out_4, AU_out_6, clock_1_out;
  wire [3:0] AU_c, demultiplexer_1_out0, demultiplexer_1_out1, LU_c, multiplexer_1_out, register_1_q,
       register_2_q, register_3_q, register_4_q;

  Register #(.width(4)) register_1 (.D(A), .en(in_2), .Q(register_1_q), .clk(clock_1_out));  // open: clr
  Register #(.width(4)) register_2 (.D(B), .en(in_2), .Q(register_2_q), .clk(clock_1_out));  // open: clr
  Clock clock_1 (.out(clock_1_out));
  LED Carry (.in(AU_out_4));
  Arithmetic AU (.A(register_1_q), .B(register_2_q), .in_2(in_7), .out_4(AU_out_4), .C(AU_c), .out_6(AU_out_6));
  Logic LU (.A(register_1_q), .B(register_2_q), .in_3(in_7), .C(LU_c));
  LED Carry_2 (.in(AU_out_6));
  Multiplexer #(.width(4), .enable("false")) multiplexer_1 (
    .in0(AU_c), .in1(LU_c), .out(multiplexer_1_out), .sel(in_5));
  Demultiplexer #(.width(4), .enable("false")) demultiplexer_1 (
    .out0(demultiplexer_1_out0), .out1(demultiplexer_1_out1), .in(multiplexer_1_out), .sel(in_5));
  Register #(.width(4)) register_3 (
    .D(demultiplexer_1_out0), .en(in_3), .Q(register_3_q), .clk(clock_1_out));  // open: clr
  Register #(.width(4)) register_4 (
    .D(demultiplexer_1_out1), .en(in_6), .Q(register_4_q), .clk(clock_1_out));  // open: clr
  DotMatrix #(.matrixcols(4), .matrixrows(1)) dotmatrix_1 (
    .col0(register_4_q[3]), .col1(register_4_q[2]), .col2(register_4_q[1]), .col3(register_4_q[0]));
  _7_segment _7_segment (
    .W(register_3_q[3]), .X(register_3_q[2]), .Y(register_3_q[1]), .Z(register_3_q[0]), .a(_7_segment_a),
    .b(_7_segment_b), .c(_7_segment_c), .d(_7_segment_d), .e(_7_segment_e), .f(_7_segment_f), .g(_7_segment_g));
  _7_Segment_Display u_7_segment_display_1 (
    .g(_7_segment_g), .f(_7_segment_f), .a(_7_segment_a), .b(_7_segment_b), .e(_7_segment_e),
    .d(_7_segment_d), .c(_7_segment_c));  // open: dp
endmodule

module _7_segment (
  input  W,
  input  X,
  input  Y,
  input  Z,
  output a,
  output b,
  output c,
  output d,
  output e,
  output f,
  output g
);

  wire and_1_out, and_2_out, and_3_out, and_4_out, and_5_out, and_6_out, and_7_out, and_8_out, and_9_out,
       and_10_out, and_11_out, and_12_out, and_13_out, and_14_out, and_15_out, and_16_out, and_17_out,
       and_18_out, and_19_out, and_20_out, and_21_out, and_22_out, and_23_out, and_24_out, and_25_out,
       and_26_out, and_27_out, and_28_out, and_29_out, and_30_out, and_31_out, and_32_out, and_33_out,
       and_34_out, and_35_out, and_36_out, not_1_out, not_2_out, not_3_out, not_4_out, not_5_out, not_6_out,
       not_7_out, not_8_out, not_9_out, not_10_out, not_11_out, not_12_out, not_13_out, not_14_out,
       not_15_out, not_16_out, not_17_out, not_18_out, not_19_out, not_20_out, not_21_out, not_22_out,
       not_23_out, not_24_out, not_25_out, not_26_out, not_27_out, not_28_out, not_29_out, not_30_out,
       not_31_out, not_32_out, not_33_out, not_34_out, not_35_out, not_36_out, not_37_out, not_38_out,
       not_39_out, not_40_out, not_41_out, not_42_out, not_43_out, not_44_out, not_45_out;

  not not_1 (not_1_out, X);
  and and_1 (and_1_out, not_1_out, not_2_out);
  not not_2 (not_2_out, Z);
  not not_3 (not_3_out, W);
  and and_2 (and_2_out, not_3_out, Y);
  not not_4 (not_4_out, W);
  and and_3 (and_3_out, not_4_out, X, Z);
  and and_4 (and_4_out, X, Y);
  and and_5 (and_5_out, W, not_5_out, not_6_out);
  not not_5 (not_5_out, X);
  not not_6 (not_6_out, Y);
  and and_6 (and_6_out, W, not_7_out);
  not not_7 (not_7_out, Z);
  not not_8 (not_8_out, W);
  and and_7 (and_7_out, not_8_out, not_9_out);
  not not_9 (not_9_out, X);
  not not_10 (not_10_out, W);
  not not_11 (not_11_out, Y);
  and and_8 (and_8_out, not_10_out, not_11_out, not_12_out);
  not not_12 (not_12_out, Z);
  not not_13 (not_13_out, X);
  and and_9 (and_9_out, not_13_out, not_14_out);
  not not_14 (not_14_out, Y);
  not not_15 (not_15_out, X);
  and and_10 (and_10_out, not_15_out, not_16_out);
  not not_16 (not_16_out, Z);
  not not_17 (not_17_out, W);
  and and_11 (and_11_out, not_17_out, Y, Z);
  not not_18 (not_18_out, Y);
  and and_12 (and_12_out, W, not_18_out, Z);
  not not_19 (not_19_out, W);
  and and_13 (and_13_out, not_19_out, not_20_out);
  not not_20 (not_20_out, Y);
  not not_21 (not_21_out, W);
  and and_14 (and_14_out, not_21_out, Z);
  not not_22 (not_22_out, Y);
  and and_15 (and_15_out, not_22_out, Z);
  not not_23 (not_23_out, W);
  and and_16 (and_16_out, not_23_out, X);
  and and_17 (and_17_out, W, not_24_out);
  not not_24 (not_24_out, X);
  not not_25 (not_25_out, W);
  and and_18 (and_18_out, not_25_out, not_26_out, not_27_out);
  not not_26 (not_26_out, X);
  not not_27 (not_27_out, Z);
  not not_28 (not_28_out, X);
  and and_19 (and_19_out, not_28_out, Y, Z);
  and and_20 (and_20_out, X, not_29_out, Z);
  not not_29 (not_29_out, Y);
  and and_21 (and_21_out, X, Y, not_30_out);
  not not_30 (not_30_out, Z);
  and and_22 (and_22_out, W, not_31_out);
  not not_31 (not_31_out, Y);
  not not_32 (not_32_out, X);
  and and_23 (and_23_out, not_32_out, not_33_out);
  not not_33 (not_33_out, Z);
  and and_24 (and_24_out, Y, not_34_out);
  not not_34 (not_34_out, Z);
  and and_25 (and_25_out, W, Y);
  and and_26 (and_26_out, W, X);
  not not_35 (not_35_out, Y);
  and and_27 (and_27_out, not_35_out, not_36_out);
  not not_36 (not_36_out, Z);
  not not_37 (not_37_out, W);
  and and_28 (and_28_out, not_37_out, X, not_38_out);
  not not_38 (not_38_out, Y);
  and and_29 (and_29_out, X, not_39_out);
  not not_39 (not_39_out, Z);
  and and_30 (and_30_out, W, not_40_out);
  not not_40 (not_40_out, X);
  and and_31 (and_31_out, W, Y);
  not not_41 (not_41_out, X);
  and and_32 (and_32_out, not_41_out, Y);
  and and_33 (and_33_out, Y, not_42_out);
  not not_42 (not_42_out, Z);
  not not_43 (not_43_out, W);
  and and_34 (and_34_out, not_43_out, X, not_44_out);
  not not_44 (not_44_out, Y);
  and and_35 (and_35_out, W, not_45_out);
  not not_45 (not_45_out, X);
  and and_36 (and_36_out, W, Z);
  or or_1 (c, and_13_out, and_14_out, and_15_out, and_16_out, and_17_out);
  or or_2 (d, and_18_out, and_19_out, and_20_out, and_21_out, and_22_out);
  or or_3 (e, and_23_out, and_24_out, and_25_out, and_26_out);
  or or_4 (f, and_27_out, and_28_out, and_29_out, and_30_out, and_31_out);
  or or_5 (g, and_32_out, and_33_out, and_34_out, and_35_out, and_36_out);
  or or_6 (a, and_1_out, and_2_out, and_3_out, and_4_out, and_5_out, and_6_out);
  or or_7 (b, and_7_out, and_8_out, and_9_out, and_10_out, and_11_out, and_12_out);
endmodule
